# Fritzing sketch V1.0 (saved by Fritzing 0.9.3b)

parts:
  MH-ET_LIVE_ESP32_DEVKIT1 = MH-ET LIVE ESP32 DEVKIT 38 pins
  Part1 = MicroSD Card Module
  ZS-042_RTC1 = ZS-042 RTC Module
  Part2 = Adafruit MAX98357A I2S 3W Class D Amplifier [part_number="Adafruit #3006"]

nets:
  3V3: MH-ET_LIVE_ESP32_DEVKIT1.3V3, Part2.VIN
  N1: MH-ET_LIVE_ESP32_DEVKIT1.IO25, Part2.DIN
  N2: MH-ET_LIVE_ESP32_DEVKIT1.IO26, Part2.BCLK
  N3: MH-ET_LIVE_ESP32_DEVKIT1.IO27, Part2.LRCLK
  N4: MH-ET_LIVE_ESP32_DEVKIT1.IO23, Part1.MOSI
  N5: MH-ET_LIVE_ESP32_DEVKIT1.IO22, ZS-042_RTC1.SCL
  N6: MH-ET_LIVE_ESP32_DEVKIT1.IO21, ZS-042_RTC1.SDA
  N7: MH-ET_LIVE_ESP32_DEVKIT1.IO19, Part1.MISO
  N8: MH-ET_LIVE_ESP32_DEVKIT1.IO18, Part1.SCK
  N9: MH-ET_LIVE_ESP32_DEVKIT1.IO5, Part1.CS

notes:
  Relay
  Current Sensor

custom parts:
  MH-ET LIVE ESP32 DEVKIT 38 pins: http://mh.nodebb.com/topic/2/mh-et-live-esp32-devkit
  Adafruit MAX98357A I2S 3W Class D Amplifier: Listen to this good news - we now have an all in one digital audio amp breakout board that works incredibly well with the Raspberry Pi! If you're looking for an easy and low cost way to get you digital sound files bumpin' then the MAX08357 I2S Amp Breakout is for you. It takes standard I2S digital audio input and, not only decodes it into analog, but also amplifies it directly into a speaker.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
